// Logisim project 1st session MERL.circ as structural Verilog
module NOT_gate (
  input  in_1,
  output out_2
);

  Transistor transistor_1 (.in(1'b1), .out(out_2), .gate(in_1));
  Transistor #(.\type ("n")) transistor_2 (.in(1'b0), .out(out_2), .gate(in_1));

  // Notes on the sheet:
  //   NOT Gate
endmodule

module AND_gate (
  input  in_1,
  input  in_2,
  output out_3
);

  wire transistor_1_out;

  Transistor #(.\type ("n")) transistor_1 (.in(1'b1), .out(transistor_1_out), .gate(in_1));
  Transistor #(.\type ("n")) transistor_2 (.in(transistor_1_out), .out(out_3), .gate(in_2));
  Transistor transistor_3 (.in(1'b0), .out(out_3), .gate(in_1));
  Transistor transistor_4 (.in(1'b0), .out(out_3), .gate(in_2));

  // Notes on the sheet:
  //   AND gate
endmodule

module NAND_gate (
  input  in_1,
  input  in_2,
  output out_3
);

  wire transistor_1_out;

  Transistor #(.\type ("n")) transistor_1 (.in(1'b0), .out(transistor_1_out), .gate(in_1));
  Transistor #(.\type ("n")) transistor_2 (.in(transistor_1_out), .out(out_3), .gate(in_2));
  Transistor transistor_3 (.in(1'b1), .out(out_3), .gate(in_1));
  Transistor transistor_4 (.in(1'b1), .out(out_3), .gate(in_2));

  // Notes on the sheet:
  //   NAND gate
endmodule

module OR_gate (
  input  in_1,
  input  in_2,
  output out_3
);

  wire transistor_1_out, transistor_2_out;

  Transistor #(.\type ("n")) transistor_1 (.in(1'b0), .out(transistor_1_out), .gate(in_1));
  Transistor transistor_2 (.in(1'b1), .out(transistor_2_out), .gate(in_1));
  Transistor transistor_3 (.in(transistor_2_out), .out(transistor_1_out), .gate(in_2));
  Transistor #(.\type ("n")) transistor_4 (.in(1'b0), .out(transistor_1_out), .gate(in_2));
  Transistor transistor_5 (.in(1'b1), .out(out_3), .gate(transistor_1_out));
  Transistor #(.\type ("n")) transistor_6 (.in(1'b0), .out(out_3), .gate(transistor_1_out));

  // Notes on the sheet:
  //   OR gate
endmodule

module NOR_gate (
  input  in_1,
  input  in_2,
  output out_3
);

  wire transistor_2_out;

  Transistor #(.\type ("n")) transistor_1 (.in(1'b0), .out(out_3), .gate(in_1));
  Transistor transistor_2 (.in(1'b1), .out(transistor_2_out), .gate(in_1));
  Transistor transistor_3 (.in(transistor_2_out), .out(out_3), .gate(in_2));
  Transistor #(.\type ("n")) transistor_4 (.in(1'b0), .out(out_3), .gate(in_2));

  // Notes on the sheet:
  //   NOR gate
endmodule

module XOR_gate (
  input  in_1,
  input  in_2,
  output out_3
);

  wire transistor_1_out;

  Transistor transistor_1 (.in(1'b1), .out(transistor_1_out), .gate(in_1));
  Transistor #(.\type ("n")) transistor_2 (.in(transistor_1_out), .out(out_3), .gate(in_1));
  Transistor transistor_3 (.in(1'b0), .out(out_3), .gate(in_1));
  Transistor #(.\type ("n")) transistor_4 (.in(1'b0), .out(out_3), .gate(in_1));

  assign in_2 = in_1;
endmodule
